// Logisim project SYL_L0_1.circ as structural Verilog: 3 circuits, main circuit main
module main (
);

  Add1Bit add1bit_1 ();  // open: A, B, C, D, C_out

  // Notes on the sheet:
  //   Attention, votre version de Logisim
  //   ne contient pas de tracker. Si vous
  //   enregistrez votre projet, toutes les
  //   informations du tracker seront
  //   définitivement effacées.
endmodule

module Add1Bit (
  input  A,
  input  B,
  input  C,
  output D,
  output C_out
);

  wire and_1_out, and_2_out, and_3_out, xor_1_out;

  xor xor_1 (xor_1_out, A, B);
  and and_1 (and_1_out, A, B);
  and and_2 (and_2_out, A, C);
  and and_3 (and_3_out, B, C);
  xor xor_2 (D, xor_1_out, C);
  or or_1 (C_out, and_1_out, and_2_out, and_3_out);

  // Notes on the sheet:
  //   Attention, votre version de Logisim
  //   ne contient pas de tracker. Si vous
  //   enregistrez votre projet, toutes les
  //   informations du tracker seront
  //   définitivement effacées.
endmodule

module Add4Bits (
  input  C,
  input  [3:0] A,
  input  [3:0] B,
  output [3:0] D,
  output C_out
);

  wire add1bit_1_c_out, add1bit_2_c_out, add1bit_3_c_out;

  Add1Bit add1bit_1 (.A(A[0]), .B(B[0]), .C(C), .D(D[0]), .C_out(add1bit_1_c_out));
  Add1Bit add1bit_2 (.A(A[1]), .B(B[1]), .C(add1bit_1_c_out), .D(D[1]), .C_out(add1bit_2_c_out));
  Add1Bit add1bit_3 (.A(A[2]), .B(B[2]), .C(add1bit_2_c_out), .D(D[2]), .C_out(add1bit_3_c_out));
  Add1Bit add1bit_4 (.A(A[3]), .B(B[3]), .C(add1bit_3_c_out), .D(D[3]), .C_out(C_out));

  // Notes on the sheet:
  //   Attention, votre version de Logisim
  //   ne contient pas de tracker. Si vous
  //   enregistrez votre projet, toutes les
  //   informations du tracker seront
  //   définitivement effacées.
endmodule
