// Logisim project labo_alu_etu.circ as structural Verilog: 9 circuits, main circuit ALU_MAXV
module ALU_MAXV (
  input  [3:0] a_i,
  input  [3:0] b_i,
  output [3:0] c_o,
  output erreur_o
);

  wire [5:0] opcode_i_sw6;

  DipSwitch opcode_i (
    .sw1(opcode_i_sw6[5]), .sw2(opcode_i_sw6[4]), .sw3(opcode_i_sw6[3]), .sw4(opcode_i_sw6[2]),
    .sw5(opcode_i_sw6[1]), .sw6(opcode_i_sw6[0]));  // open: sw7, sw8
  ALU_Top alu_inst (.a_i(a_i), .b_i(b_i), .op_i(opcode_i_sw6), .c_o(c_o), .erreur_o(erreur_o));

  // Notes on the sheet:
  //   Attention, votre version de Logisim
  //   ne contient pas de tracker. Si vous
  //   enregistrez votre projet, toutes les
  //   informations du tracker seront
  //   définitivement effacées.
endmodule

module ALU_Top (
  input  [3:0] a_i,
  input  [3:0] b_i,
  input  [5:0] op_i,
  output [3:0] c_o,
  output erreur_o
);

  wire c, n, v, z;
  wire [3:0] alu_addsub4bit_1_r_o, alu_comparator_1_cmp_o, alu_custom_1_s_o, alu_logicunit_1_f_o;

  ALU_Custom alu_custom_1 (.a_i(a_i), .s_o(alu_custom_1_s_o));
  ALU_AddSub4bit alu_addsub4bit_1 (
    .a_i(a_i), .b_i(b_i), .op_i(op_i[3:2]), .r_o(alu_addsub4bit_1_r_o), .overflow_o(v), .carry_o(c),
    .zero_o(z), .negative_o(n));
  ALU_Comparator alu_comparator_1 (
    .op_i(op_i[2:0]), .negative_i(n), .zero_i(z), .carry_i(c), .cmp_o(alu_comparator_1_cmp_o));
  ALU_LogicUnit alu_logicunit_1 (.a_i(a_i), .b_i(b_i), .op_i(op_i[1:0]), .f_o(alu_logicunit_1_f_o));
  Multiplexer #(.select(2), .width(4), .enable("false")) multiplexer_1 (
    .in0(alu_addsub4bit_1_r_o), .in1(alu_comparator_1_cmp_o), .in2(alu_logicunit_1_f_o),
    .in3(alu_custom_1_s_o), .out(c_o), .sel(op_i[5:4]));
  ALU_ErrorCheck alu_errorcheck_1 (.op_sel_i(op_i[5:4]), .overflow_i(v), .op_param_i(op_i[3:0]), .error_o(erreur_o));

  // Notes on the sheet:
  //   Attention, votre version de Logisim
  //   ne contient pas de tracker. Si vous
  //   enregistrez votre projet, toutes les
  //   informations du tracker seront
  //   définitivement effacées.
endmodule

module Add1bit (
  input  a_i,
  input  b_i,
  input  c_i,
  output r_o,
  output c_o
);

  wire and_1_out, and_2_out, xor_1_out;

  xor xor_1 (xor_1_out, a_i, b_i);
  and and_1 (and_1_out, xor_1_out, c_i);
  and and_2 (and_2_out, a_i, b_i);
  xor xor_2 (r_o, xor_1_out, c_i);
  or or_1 (c_o, and_1_out, and_2_out);

  // Notes on the sheet:
  //   Attention, votre version de Logisim
  //   ne contient pas de tracker. Si vous
  //   enregistrez votre projet, toutes les
  //   informations du tracker seront
  //   définitivement effacées.
endmodule

module Add4bit (
  input  c_i,
  input  [3:0] a_i,
  input  [3:0] b_i,
  output [3:0] r_o,
  output c_o
);

  wire add1bit_1_c_o, add1bit_2_c_o, add1bit_3_c_o;

  Add1bit add1bit_1 (.a_i(a_i[0]), .b_i(b_i[0]), .c_i(c_i), .r_o(r_o[0]), .c_o(add1bit_1_c_o));
  Add1bit add1bit_2 (.a_i(a_i[1]), .b_i(b_i[1]), .c_i(add1bit_1_c_o), .r_o(r_o[1]), .c_o(add1bit_2_c_o));
  Add1bit add1bit_3 (.a_i(a_i[2]), .b_i(b_i[2]), .c_i(add1bit_2_c_o), .r_o(r_o[2]), .c_o(add1bit_3_c_o));
  Add1bit add1bit_4 (.a_i(a_i[3]), .b_i(b_i[3]), .c_i(add1bit_3_c_o), .r_o(r_o[3]), .c_o(c_o));

  // Notes on the sheet:
  //   Attention, votre version de Logisim
  //   ne contient pas de tracker. Si vous
  //   enregistrez votre projet, toutes les
  //   informations du tracker seront
  //   définitivement effacées.
endmodule

module ALU_AddSub4bit (
  input  [3:0] a_i,
  input  [3:0] b_i,
  input  [1:0] op_i,
  output [3:0] r_o,
  output overflow_o,
  output carry_o,
  output zero_o,
  output negative_o
);

  wire and_2_out, and_3_out, or_1_out, xor_2_out, xor_3_out;
  wire [3:0] xor_1_out;

  // Probe on op_i[1]
  // Probe on op_i[0]
  assign xor_1_out = b_i ^ {4{op_i[1]}};  // XOR_Gate xor_1, 4 bits wide
  Add4bit add4bit_1 (.c_i(op_i[1]), .a_i(a_i), .b_i(xor_1_out), .r_o(r_o), .c_o(carry_o));
  nor nor_1 (zero_o, r_o[3], r_o[2], r_o[1], r_o[0]);
  xor xor_2 (xor_2_out, r_o[3], overflow_o);
  and and_1 (negative_o, ~op_i[0], xor_2_out);  // AND_Gate
  and and_2 (and_2_out, a_i[3], xor_1_out[3], ~r_o[3]);  // AND_Gate
  and and_3 (and_3_out, ~a_i[3], ~xor_1_out[3], r_o[3]);  // AND_Gate
  xor xor_3 (xor_3_out, op_i[1], carry_o);
  or or_1 (or_1_out, and_2_out, and_3_out);
  Multiplexer #(.enable("false")) multiplexer_1 (.in0(or_1_out), .in1(xor_3_out), .out(overflow_o), .sel(op_i[0]));

  // Notes on the sheet:
  //   Attention, votre version de Logisim
  //   ne contient pas de tracker. Si vous
  //   enregistrez votre projet, toutes les
  //   informations du tracker seront
  //   définitivement effacées.
endmodule

module ALU_Comparator (
  input  [2:0] op_i,
  input  negative_i,
  input  zero_i,
  input  carry_i,
  output [3:0] cmp_o
);

  wire not_1_out, not_2_out, not_3_out;

  not not_1 (not_1_out, negative_i);
  not not_2 (not_2_out, zero_i);
  not not_3 (not_3_out, carry_i);
  Multiplexer #(.select(3), .enable("false")) multiplexer_1 (
    .in0(1'b0), .in1(not_1_out), .in2(negative_i), .in3(not_2_out), .in4(zero_i), .in5(carry_i),
    .in6(not_3_out), .in7(1'b0), .out(cmp_o[0]), .sel(op_i));

  assign cmp_o[3:1] = 3'b000;

  // Notes on the sheet:
  //   Attention, votre version de Logisim
  //   ne contient pas de tracker. Si vous
  //   enregistrez votre projet, toutes les
  //   informations du tracker seront
  //   définitivement effacées.
endmodule

module ALU_LogicUnit (
  input  [3:0] a_i,
  input  [3:0] b_i,
  input  [1:0] op_i,
  output [3:0] f_o
);

  wire [3:0] and_1_out, not_1_out, or_1_out, xor_1_out;

  assign and_1_out = a_i & b_i;  // AND_Gate and_1, 4 bits wide
  assign or_1_out = a_i | b_i;  // OR_Gate or_1, 4 bits wide
  assign xor_1_out = a_i ^ b_i;  // XOR_Gate xor_1, 4 bits wide
  assign not_1_out = ~and_1_out;  // NOT_Gate not_1, 4 bits wide
  Multiplexer #(.select(2), .width(4), .enable("false")) multiplexer_1 (
    .in0(and_1_out), .in1(or_1_out), .in2(not_1_out), .in3(xor_1_out), .out(f_o), .sel(op_i));

  // Notes on the sheet:
  //   Attention, votre version de Logisim
  //   ne contient pas de tracker. Si vous
  //   enregistrez votre projet, toutes les
  //   informations du tracker seront
  //   définitivement effacées.
endmodule

module ALU_Custom (
  input  [3:0] a_i,
  output [3:0] s_o
);

  wire or_1_out, xor_2_out;

  xor xor_1 (s_o[0], a_i[0], a_i[1], a_i[2], a_i[3]);
  ExactlyOne xor_2 (.out(xor_2_out), .in0(a_i[0]), .in1(a_i[1]), .in2(a_i[2]), .in3(a_i[3]));
  or or_1 (or_1_out, a_i[0], a_i[1], a_i[2], a_i[3]);
  and and_1 (s_o[2], a_i[0], a_i[1], a_i[2], a_i[3]);
  and and_2 (s_o[1], ~xor_2_out, or_1_out, ~s_o[2]);  // AND_Gate

  assign s_o[3] = 1'b0;

  // Notes on the sheet:
  //   Attention, votre version de Logisim
  //   ne contient pas de tracker. Si vous
  //   enregistrez votre projet, toutes les
  //   informations du tracker seront
  //   définitivement effacées.
endmodule

module ALU_ErrorCheck (
  input  [1:0] op_sel_i,
  input  overflow_i,
  input  [3:0] op_param_i,
  output error_o
);

  wire and_1_out, and_2_out, or_1_out;

  and and_1 (and_1_out, op_param_i[0], op_param_i[1], op_param_i[2]);
  and and_2 (and_2_out, ~op_param_i[0], ~op_param_i[1], ~op_param_i[2]);  // AND_Gate
  or or_1 (or_1_out, and_1_out, and_2_out, ~op_param_i[3]);  // OR_Gate
  Multiplexer #(.select(2), .enable("false")) multiplexer_1 (
    .in0(overflow_i), .in1(or_1_out), .in2(1'b0), .in3(1'b0), .out(error_o), .sel(op_sel_i));

  // Notes on the sheet:
  //   Attention, votre version de Logisim
  //   ne contient pas de tracker. Si vous
  //   enregistrez votre projet, toutes les
  //   informations du tracker seront
  //   définitivement effacées.
endmodule
